# Fritzing sketch fritzingDoCarrinho (saved by Fritzing 0.9.3b)
breadboards: 1

parts:
  L298N1 = L298N DC motor driver
  Componente1 = Arduino Nano (Rev3.0)
  M1 = DC Motor
  M2 = DC Motor
  M3 = DC Motor
  M4 = DC Motor
  BAT1 = Battery Holders [package=lipo-1100mAh]  # not connected
  U1 = LIPO-1000mAh [package=lipo-1000]
  Componente2 = Bluetooth HC-05 Macho

nets:
  N1: L298N1.12V, U1.+
  N2: L298N1.ENA, Componente1.D10
  N3: L298N1.ENB, Componente1.D5
  N4: L298N1.IN1, Componente1.D9
  N5: L298N1.IN2, Componente1.D8
  N6: L298N1.IN3, Componente1.D7
  N7: L298N1.IN4, Componente1.D6
  N8: Componente1.D1/TX, Componente2.RXD
  N9: Componente1.D0/RX, Componente2.TXD
  GND: Componente1.GND, Componente2.GND
  VIN: Componente1.VIN, Componente2.VCC
  N10: M1.pin_1, M2.pin_1
  N11: M1.pin_2, M2.pin_2
  N12: M3.pin_1, M4.pin_1
  N13: M3.pin_2, M4.pin_2

custom parts:
  L298N DC motor driver: 2x DC motor driver with 78M05 positive voltage regulator (7..35 V) L298N: max 46 V, 2 A Set 5 V Enable jumper to enable 5 V regultor (needed for the L298N) and +5 V output at screw terminal or supply external +5 V at screw terminal Set ENA and/or ENB to +5 V to enable motor permanently or supply ENA and/or ENB with PWM signal IN1 and IN2 set rotation directory for motor A (OUT1/OUT2) IN2 and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
